// Logisim project async_counter_3bits.circ as structural Verilog: 1 circuit, main circuit counter
module counter (
);

  wire bcd_7seg_rom_dec_1_a_2, bcd_7seg_rom_dec_1_b_2, bcd_7seg_rom_dec_1_c_2, bcd_7seg_rom_dec_1_d_2,
       bcd_7seg_rom_dec_1_e, bcd_7seg_rom_dec_1_f, bcd_7seg_rom_dec_1_g, clock_1_out, j_k_ff_1_q,
       j_k_ff_1_qn, j_k_ff_2_q, j_k_ff_2_qn, j_k_ff_3_q;

  Clock clock_1 (.out(clock_1_out));
  J_K_Flip_Flop j_k_ff_1 (
    .J(1'b1), .clk(clock_1_out), .K(1'b1), .Q(j_k_ff_1_q), .Qn(j_k_ff_1_qn), .preset(1'b0), .en(1'b1),
    .reset(1'b0));
  J_K_Flip_Flop j_k_ff_2 (
    .J(1'b1), .clk(j_k_ff_1_qn), .K(1'b1), .Q(j_k_ff_2_q), .Qn(j_k_ff_2_qn), .preset(1'b0), .en(1'b1),
    .reset(1'b0));
  J_K_Flip_Flop j_k_ff_3 (
    .J(1'b1), .clk(j_k_ff_2_qn), .K(1'b1), .Q(j_k_ff_3_q), .preset(1'b0), .en(1'b1), .reset(1'b0));  // open: Qn
  bcd_7seg_rom_dec bcd_7seg_rom_dec_1 (
    .A(j_k_ff_1_q), .B(j_k_ff_2_q), .C(j_k_ff_3_q), .D(1'b0), .e(bcd_7seg_rom_dec_1_e),
    .d_2(bcd_7seg_rom_dec_1_d_2), .c_2(bcd_7seg_rom_dec_1_c_2), .b_2(bcd_7seg_rom_dec_1_b_2),
    .a_2(bcd_7seg_rom_dec_1_a_2), .f(bcd_7seg_rom_dec_1_f), .g(bcd_7seg_rom_dec_1_g));
  _7_Segment_Display #(.active("false")) u_7_segment_display_1 (
    .g(bcd_7seg_rom_dec_1_g), .f(bcd_7seg_rom_dec_1_f), .a(bcd_7seg_rom_dec_1_a_2),
    .b(bcd_7seg_rom_dec_1_b_2), .e(bcd_7seg_rom_dec_1_e), .d(bcd_7seg_rom_dec_1_d_2),
    .c(bcd_7seg_rom_dec_1_c_2), .dp(1'b1));
endmodule
