// Logisim project bcd_7seg_dec_rom.circ as structural Verilog: 2 circuits, main circuit bcd_7seg_dec_rom
module bcd_7seg_dec_rom (
  input  A,
  input  B,
  input  C,
  input  D,
  output a_2,
  output b_2,
  output c_2,
  output d_2,
  output e,
  output f,
  output g
);

  ROM #(.addrWidth(4), .dataWidth(7)) rom_1 (.addr({D, C, B, A}), .data({a_2, b_2, c_2, d_2, e, f, g}));  // open: sel

  // Notes on the sheet:
  //   contents of rom_1 (hex, n*v repeats v):
  //   1 67 12 42 64 48 c 63 0 60 1e 4e 74 58 1c 7f
endmodule

module bcd_7seg_dec (
  input  in_1,
  input  in_2,
  input  in_3,
  input  in_4
);

  wire bcd_7seg_dec_rom_1_a_2, bcd_7seg_dec_rom_1_b_2, bcd_7seg_dec_rom_1_c_2, bcd_7seg_dec_rom_1_d_2,
       bcd_7seg_dec_rom_1_e, bcd_7seg_dec_rom_1_f, bcd_7seg_dec_rom_1_g;

  bcd_7seg_dec_rom bcd_7seg_dec_rom_1 (
    .A(in_1), .B(in_2), .C(in_3), .D(in_4), .a_2(bcd_7seg_dec_rom_1_a_2), .b_2(bcd_7seg_dec_rom_1_b_2),
    .c_2(bcd_7seg_dec_rom_1_c_2), .d_2(bcd_7seg_dec_rom_1_d_2), .e(bcd_7seg_dec_rom_1_e),
    .f(bcd_7seg_dec_rom_1_f), .g(bcd_7seg_dec_rom_1_g));
  _7_Segment_Display #(.active("false")) u_7_segment_display_1 (
    .g(bcd_7seg_dec_rom_1_g), .f(bcd_7seg_dec_rom_1_f), .a(bcd_7seg_dec_rom_1_e), .b(bcd_7seg_dec_rom_1_d_2),
    .e(bcd_7seg_dec_rom_1_a_2), .d(bcd_7seg_dec_rom_1_b_2), .c(bcd_7seg_dec_rom_1_c_2), .dp(1'b1));
endmodule
